# Fritzing sketch WorldMap (saved by Fritzing 0.9.10b)

parts:
  WeMos_D1_Mini1 = WeMos D1 Mini
  Part1 = TXB0108 8-channel Bi-directional Logic Level Converter
  LED5 = LED - 5mm [color="White (4500K)" current=0.030 package="5 mm [THT]"]
  U1 = POT [knob_status=50% power=0.5W package=pot_alpha_rv16af-20]
  Mod1 = KY-003 Hall Magnetic Sensor Module [package="Breakout board"]
  Mod2 = KY-003 Hall Magnetic Sensor Module [package="Breakout board"]
  Mod3 = KY-003 Hall Magnetic Sensor Module [package="Breakout board"]
  Mod4 = KY-003 Hall Magnetic Sensor Module [package="Breakout board"]
  Mod5 = KY-003 Hall Magnetic Sensor Module [package="Breakout board"]
  LED6 = LED - 5mm [color="White (4500K)" current=0.030 package="5 mm [THT]"]
  LED7 = LED - 5mm [color="White (4500K)" current=0.030 package="5 mm [THT]"]
  LED8 = LED - 5mm [color="White (4500K)" current=0.030 package="5 mm [THT]"]
  LED9 = LED - 5mm [color="White (4500K)" current=0.030 package="5 mm [THT]"]
  R2 = Resistor [tolerance=±5% resistance=220 package="0603 [SMD]"]

nets:
  N1: WeMos_D1_Mini1.3V3, Part1.VCCB
  VIN: WeMos_D1_Mini1.5V, Part1.VCCA, Mod1.Vin, Mod2.Vin, Mod3.Vin, Mod4.Vin, Mod5.Vin
  N2: WeMos_D1_Mini1.D0, Part1.B2
  N3: WeMos_D1_Mini1.D4, Part1.B1
  N4: WeMos_D1_Mini1.D5, Part1.B3
  N5: WeMos_D1_Mini1.D6, Part1.B4
  N6: WeMos_D1_Mini1.D7, Part1.B5
  N7: WeMos_D1_Mini1.D8, Part1.B6
  N8: WeMos_D1_Mini1.G, Part1.GND, LED5.cathode, Mod1.-, Mod2.-, Mod3.-, Mod4.-, Mod5.-, LED6.cathode, LED7.cathode, LED8.cathode, LED9.cathode
  N9: Part1.A6, R2.Pin_1
  N10: Part1.A5, Mod5.S
  N11: Part1.A4, Mod4.S
  N12: Part1.A3, Mod3.S
  N13: Part1.A2, Mod2.S
  N14: Part1.A1, Mod1.S
  N15: LED5.anode, U1.A, LED6.anode, LED7.anode, LED8.anode, LED9.anode
  N16: U1.S, R2.Pin_0

custom parts:
  TXB0108 8-channel Bi-directional Logic Level Converter: Because the Arduino (and Basic Stamp) are 5V devices, and most modern sensors, displays, flash cards and modes are 3.3V-only, many makers find that they need to perform level shifting/conversion to protect the 3.3V device from 5V. Although one can use resistors to make a divider, for high speed transfers, the resistors can add a lot of slew and cause havoc that is tough to debug. For that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
  KY-003 Hall Magnetic Sensor Module: KEYES KY-003 Arduino Hall Magnetic Sensor Module is a switch that will turn on/off in the presence of a magnetic field.
